# Fritzing sketch LuckNert_Firebase (saved by Fritzing 0.9.3b)

parts:
  WeMos_D1_Mini1 = WeMos D1 Mini
  Capacitive_Soil_Moisture_Sensor1 = DFRobot Capacitive Soil Moisture Sensor V1.0 [part_number=SEN0193]
  DHT1 = Humidity and Temperature Sensor DHT11
  Part3 = Lilypad Battery Connect
  KY-2 = Keyes Relay [package=THT]
  LCD2 = LCD screen
  LCM1602_IIC2 = LCM1602 IIC [part_number="LCM1602 IIC" chip_label="LCM1602 IIC" package="DIP (Dual Inline) [THT]"]

nets:
  VCC: WeMos_D1_Mini1.5V, Capacitive_Soil_Moisture_Sensor1.VCC, DHT1.Data-signal, KY-2.power, LCM1602_IIC2.VCC
  N1: WeMos_D1_Mini1.A0, Capacitive_Soil_Moisture_Sensor1.A
  N2: WeMos_D1_Mini1.D0, KY-2.signal
  N3: WeMos_D1_Mini1.D1, LCM1602_IIC2.SCL
  N4: WeMos_D1_Mini1.D2, LCM1602_IIC2.SDA
  N5: WeMos_D1_Mini1.D3, DHT1.Vcc
  GND: WeMos_D1_Mini1.G, Capacitive_Soil_Moisture_Sensor1.GND, DHT1.GND_1, KY-2.ground, LCM1602_IIC2.GND
  N6: Part3.-, KY-2.C
  N7: LCD2.DB4, LCM1602_IIC2.D4
  N8: LCD2.DB5, LCM1602_IIC2.D5
  N9: LCD2.DB6, LCM1602_IIC2.D6
  N10: LCD2.DB7, LCM1602_IIC2.D7
  N11: LCD2.LED+, LCM1602_IIC2.A
  N12: LCD2.LED-, LCM1602_IIC2.K
  N13: LCM1602_IIC2.LED_A, LCM1602_IIC2.LED_B

notes:
  Out 220v
  ------------
  In 220v
  ----------

custom parts:
  DFRobot Capacitive Soil Moisture Sensor V1.0: DFRobot Capacitive Soil Moisture Sensor V1.0 This product measures soil moisture levels by capacitive sensing, rather than resistive sensing like other types of moisture sensor. It is made of a corrosion resistant material giving it a long service life. Insert it into soil and impress your friends with the real-time soil moisture data! The product includes an on-board voltage regulator which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
  Humidity and Temperature Sensor DHT11: Digital relative humidity & temperature sensor DHT11
  Keyes Relay: The Keyes 5V relay module is suitable for SCM development, home appliance control. It uses a 5V~12V TIL control signal which can control DC / AC signal.
  LCM1602 IIC: I2C-Module to use a 1602 or 2004 LCD on with the wire.h libory Serial LCD Modul

// code stored in the sketch: LuckNet_Firebase.ino
/*
	Caranya
	------------------------------------------------------------------------
	1. Unduh dan daftar aplikasi disini https://luck-net.web.app
	2. Buka aplikasi dan klik ikon tombol setelan dikiri atas & tempel UID anda
	4. Unduh libraries https://github.com/CusMeDroid/Arduino
	3. Hubungkan papan dan unggah
	Selamat mencoba
	------------------------------------------------------------------------
	~ Suryo Dwijayanto
*/

#include <ESP8266WiFi.h>
#include <KSmart_LCDI2C.h>
#include <KSmart_Firebase.h>
#include <DHT.h>

KSmart_LCDI2C lcd(0x27, 16, 2); // SCL D1 SDA D2

#define KSmart_SSID "LuckNet" // Penambatan WiFi SSID
#define KSmart_PASSWORD "Demo12345678" // Penambatan WiFi Kata Sandi

#define DHTPIN D3
#define DHTTYPE DHT11
DHT dht(DHTPIN, DHTTYPE);

#define KSmart_RELAY D0

// Pin untuk sensor kelembaban tanah (sesuaikan dengan pin analog yang Anda gunakan)
const int soilMoisturePin = A0;

#define KSmart_URL "https://luck-net-default-rtdb.asia-southeast1.firebasedatabase.app/"

// ----------------- UID --------------------
String KSmart_UID = "TEMPEL_UID_ANDA_DISINI";
// ----------------- UID --------------------

String KSmart_UNIQ = "users/" + KSmart_UID;

Firebase firebase(KSmart_URL);

void setup() {
  lcd.init();
  lcd.noBacklight();
  
  Serial.begin(115200);
  pinMode(KSmart_RELAY, OUTPUT);
  digitalWrite(KSmart_RELAY, 0);
  WiFi.mode(WIFI_STA);
  WiFi.disconnect();
  // delay(1000);

  // Connect to WiFi
  Serial.println("");
  Serial.println("");
  Serial.print("Connecting to: ");
  Serial.println(KSmart_SSID);
  WiFi.begin(KSmart_SSID, KSmart_PASSWORD);

  while (WiFi.status() != WL_CONNECTED) {
    delay(500);
    Serial.print("-");
  }

  Serial.println("");
  Serial.println("WiFi Connected!");
  
  dht.begin();
  lcd.init();
  lcd.backlight();
  lcd.setCursor(0, 0);
  lcd.print(firebase.getString(KSmart_UNIQ + "/title"));
  lcd.setCursor(0, 1);
  lcd.print(firebase.getString(KSmart_UNIQ + "/description"));
}

String data_relay;
String data_auto;
String xon = "on";
String xoff = "off";
String xTitle;
    
void loop() {
  lcd.init();
  
  // Baca data dari sensor DHT
  float humidity = dht.readHumidity();
  float temperature = dht.readTemperature(); // Anda mungkin perlu readTemperature(unit) untuk Celcius/Fahrenheit
  
  // Periksa kesalahan pembacaan
  if (isnan(humidity) || isnan(temperature)) {
    Serial.println("Failed to read from DHT sensor!");
  } else {
    // Kirim data ke Firebase
    firebase.setString(KSmart_UNIQ + "/humidity", String(humidity));
    firebase.setString(KSmart_UNIQ + "/temperature", String(temperature));
    Serial.print("Humidity: ");
    Serial.print(humidity);
    Serial.print(" %\t");
    Serial.print("Temperature: ");
    Serial.print(temperature);
    Serial.println(" °C");
  }
  
  data_relay = firebase.getString(KSmart_UNIQ + "/relay");
  if (data_relay == "on") {
    digitalWrite(KSmart_RELAY, 1);
    xTitle = firebase.getString(KSmart_UNIQ + "/title")+" - ON ";
    Serial.println("Relay On");
  } else if (data_relay == "off") {
    digitalWrite(KSmart_RELAY, 0);
    xTitle = firebase.getString(KSmart_UNIQ + "/title")+" - OFF ";
    Serial.println("Relay Off");
  }

  // Baca data dari sensor kelembaban tanah
  int soilMoistureValue = analogRead(soilMoisturePin);

  // Mapping nilai analog ke rentang 0-100%
  float soilMoisturePercentage = map(soilMoistureValue, 0, 1023, 0, 100);

  // Kirim data ke Firebase
  firebase.setFloat(KSmart_UNIQ + "/soilmoisture", soilMoisturePercentage);

  Serial.print("Soil Moisture Analog: ");
  Serial.print(soilMoisturePercentage);
  Serial.print(" %\t");
  
  // Auto On
  data_auto = firebase.getString(KSmart_UNIQ + "/auto");
  if (data_auto == "on"){
    Serial.println("Set auto on");
    String data_sm_value = firebase.getString(KSmart_UNIQ + "/sm_value");
    int xxdtr = data_sm_value.toInt();
    Serial.println(xxdtr);
    // Kontrol Relay berdasarkan data ANALOG (jika data digital tidak reliabel)
    if (soilMoisturePercentage < xxdtr) { // Sesuaikan ambang batas kelembaban
      digitalWrite(KSmart_RELAY, 0); // Relay OFF
      xTitle = firebase.getString(KSmart_UNIQ + "/title")+" - OFF ";
      firebase.setString(KSmart_UNIQ + "/relay", String(xoff));
      Serial.println("Relay OFF (Tanah Basah - Data Analog)");
    } else if (soilMoisturePercentage > xxdtr) {
      digitalWrite(KSmart_RELAY, 1); // Relay ON
      xTitle = firebase.getString(KSmart_UNIQ + "/title")+" - ON ";
      firebase.setString(KSmart_UNIQ + "/relay", String(xon));
      Serial.println("Relay ON (Tanah Kering - Data Analog)");
    }
  } else if (data_auto == "off") {
    Serial.println("Set auto off");
  }
  
  lcd.setCursor(0, 0);
  lcd.print(xTitle);
  lcd.setCursor(0, 1);
  
  // Format floats for LCD using sprintf
  char buffer[16]; // Adjust size as needed
  sprintf(buffer, "%d%% %dC %d%%", (int)humidity, (int)temperature, (int)soilMoisturePercentage);
  lcd.print(buffer);
}
